# Fritzing sketch ex01_01 02 03 Nano layout (saved by Fritzing 0.9.10b)
breadboards: 2

parts:
  Part1 = Arduino Nano (Rev3.0)
  Part2 = Arduino Nano (Rev3.0)
  R1 = Resistor [tolerance=±5% power=0.25 resistance=220 package=THT]
  R2 = Resistor [tolerance=±5% power=0.25 resistance=220 package=THT]
  S1 = Pushbutton [package=THT]
  S2 = Pushbutton [package=THT]
  LED1 = LED - 5mm [color="Red (633nm)" current=0.030 package="5 mm [THT]"]
  LED2 = LED - 5mm [color="Red (633nm)" current=0.030 package="5 mm [THT]"]
  R3 = Resistor [tolerance=±5% power=0.25 resistance=220 package=THT]
  LED3 = LED - 5mm [color="Red (633nm)" current=0.030 package="5 mm [THT]"]
  LED4 = LED - 5mm [color="Red (633nm)" current=0.030 package="5 mm [THT]"]
  R4 = Resistor [tolerance=±5% power=0.25 resistance=220 package=THT]

nets:
  GND: Part1.GND, Part2.GND, Part2.D6, S1.leg1, S2.leg1, LED1.anode, LED3.anode, LED4.anode
  N1: Part1.D2, R2.Pin_0
  N2: Part1.D3, R3.Pin_0
  N3: Part1.D4, S1.leg0
  N4: Part1.D5, S2.leg0
  N5: Part2.D2, R4.Pin_0
  N6: Part2.D3, R1.Pin_0
  N7: R1.Pin_1, LED4.cathode
  N8: R2.Pin_1, LED2.cathode
  N9: LED1.cathode, R4.Pin_1
