# Fritzing sketch ex03_02_2_buttons_2_switches (saved by Fritzing 0.9.2b)
breadboards: 1

parts:
  Part1 = Arduino Nano (Rev3.0)
  R1 = Resistor [tolerance=±5% resistance=220 package=THT]
  R2 = Resistor [tolerance=±5% resistance=220 package=THT]
  LED1 = LEDs [package=led10mm]
  LED2 = LEDs [package=led10mm]
  S1 = Round Pushbutton
  S2 = Round Pushbutton

nets:
  N1: Part1.GND, LED1.C, LED2.C, S1.leg1, S2.leg0
  N2: Part1.D2, R1.Pin_0
  N3: Part1.D3, R2.Pin_0
  N4: Part1.D4, S2.leg1
  N5: Part1.D5, S1.leg0
  N6: R1.Pin_1, LED2.A
  N7: R2.Pin_1, LED1.A
